# Fritzing sketch fritzing (saved by Fritzing 0.9.3b)

parts:
  M1 = DC Motor
  M2 = DC Motor
  Parça4 = Arduino Uno (Rev3) - ICSP
  S1 = H-Bridge with L298N
  BAT1 = BC9VPC [package=bc9vpc]  # not connected
  VCC1 = 4 x AAA Battery Mount
  hc-sr1 = hc-sr04

nets:
  N1: M1.pin_1, S1.OUT4-Motor2
  N2: M1.pin_2, S1.OUT3-Motor2
  N3: M2.pin_1, S1.OUT1-Motor1
  N4: M2.pin_2, S1.OUT2-Motor1
  N5: Parça4.ICSP_MISO, Parça4.D12/MISO, S1.IN2
  N6: Parça4.D10_PWM/SS, S1.IN4
  N7: Parça4.D11_PWM/MOSI, S1.IN3
  N8: Parça4.D13/SCK, S1.IN1
  GND: Parça4.GND, S1.GND, VCC1.-, hc-sr1.GND
  N9: Parça4.D1/TX, hc-sr1.Echo
  N10: Parça4.D2, hc-sr1.Trig
  5V: Parça4.5V, hc-sr1.VCC
  N11: S1.12V, VCC1.+

custom parts:
  H-Bridge with L298N: h-bridge
