# Fritzing sketch esquema_dispensador_gel (saved by Fritzing 0.9.3b)

parts:
  Relay = CAR RELAY [part_number=NVF4-2 package=THT]  # not connected
  M1 = DC Motor
  VCC1 = Battery
  Componente5 = Arduino Uno (Rev3)
  hc-sr1 = hc-sr04

nets:
  N1: M1.pin_1, VCC1.+
  N2: Componente5.D12/MISO, hc-sr1.Echo
  N3: Componente5.D13/SCK, hc-sr1.Trig
  GND: Componente5.GND, hc-sr1.GND
  5V: Componente5.5V, hc-sr1.VCC

notes:
  NC
  COM
  NO
  S
  +
  -
