# Fritzing sketch fritzing-led (saved by Fritzing 0.9.3b)
breadboards: 1

parts:
  Arduino1 = Arduino Uno (Rev3)
  hc-sr1 = hc-sr04
  LED1 = LED - 5mm [color="Red (633nm)" package="5 mm [THT]"]
  R1 = Resistor [tolerance=±5% resistance=220 package=THT]

nets:
  N1: Arduino1.D12/MISO, hc-sr1.Echo
  N2: Arduino1.D13/SCK, hc-sr1.Trig
  GND: Arduino1.GND, hc-sr1.GND, LED1.cathode
  N3: Arduino1.D3_PWM, R1.Pin_1
  5V: Arduino1.5V, hc-sr1.VCC
  N4: LED1.anode, R1.Pin_0
