# Fritzing sketch esquema_maceta (saved by Fritzing 0.9.3b)

parts:
  Relay = CAR RELAY [part_number=NVF4-2 package=THT]  # not connected
  M1 = DC Motor
  VCC1 = Battery
  Componente5 = Arduino Uno (Rev3)
  부품3 = FC-28 Soil Hygrometer Module
  부품4 = FC-28 Soil Hygrometer Module - Probe

nets:
  N1: M1.pin_1, VCC1.+
  GND: Componente5.GND, 부품3.GND
  5V: Componente5.5V, 부품3.VCC
  N2: 부품3.POS, 부품4.POS
  N3: 부품3.NEG, 부품4.NEG

notes:
  NC
  COM
  NO
  S
  +
  -

custom parts:
  FC-28 Soil Hygrometer Module: The FC-28 is a soil hygrometer module that uses the Texas Instruments LM393 comparator chip to provide an analog measurement of soil humidity. The digital output is high when soil moisture is over a certain threshold, as determined by adjusting the potentiometer.
  FC-28 Soil Hygrometer Module - Probe: The FC-28 is a soil hygrometer module that uses the Texas Instruments LM393 comparator chip to provide an analog measurement of soil humidity.
